# Fritzing sketch Weather Stn R 1.4 (saved by Fritzing 0.9.3b)
circuit board: 8.5cm x 6.5cm
breadboards: 4

parts:
  PWR = LED - 5mm [color="Red (633nm)" package="5 mm [THT]"]  # not connected
  TNSMT = LED - 5mm [color="Green (560nm)" package="5 mm [THT]"]  # not connected
  BMP280 = female pin header, 4 pins [form="♀ (female)"]
  BMP280_2 = BME280 Breakout  # not connected
  UV = female pin header, 4 pins [form="♀ (female)"]
  PWR_LED = female pin header, 2 pins [form="♀ (female)"]
  Tx_LED = female pin header, 2 pins [form="♀ (female)"]
  R6 = Resistor [tolerance=±5% resistance=150 package=THT]
  Rain = female pin header, 3 pins [form="♀ (female)"]
  W_Dir = female pin header, 3 pins [form="♀ (female)"]
  Rain_2 = HALL-EFFECT [package=sc70]  # not connected
  3_3V = Voltage Regulator - Variable [package="TO220 [THT]"]
  R1 = Resistor [tolerance=±5% resistance=270 package=THT]
  Wind = HALL-EFFECT [package=sc70]  # not connected
  Wind_2 = female pin header, 3 pins [form="♀ (female)"]
  C2 = Electrolytic Capacitor [capacitance=1µF package="100 mil [THT, electrolytic]"]
  R2 = Trimmer Potentiometer [maximum_resistance=10kΩ package=THT]
  R9 = Resistor [tolerance=±5% resistance=10k package=THT]
  R8 = Resistor [tolerance=±5% resistance=10k package=THT]
  5v = Voltage Regulator - 5V [package="TO220 [THT]"]
  C1 = Electrolytic Capacitor [capacitance=10µF package="100 mil [THT, electrolytic]"]
  R5 = Resistor [tolerance=±5% resistance=10k package=THT]
  Arduino_Nano = Arduino Nano (Rev3.0)
  UART = male pin header, 3 pins [form="♂ (male)"]
  S1 = Pushbutton [package=THT]  # not connected
  RST = female pin header, 2 pins [form="♀ (female)"]
  ESP_8266 = ESP8266 WiFi Module [part_number=ESP8266]
  R7 = Resistor [tolerance=±5% resistance=150 package=THT]
  R4 = Trimmer Potentiometer [maximum_resistance=10kΩ package=THT]
  C4 = Electrolytic Capacitor [capacitance=1µF package="100 mil [THT, electrolytic]"]
  R3 = Resistor [tolerance=±5% resistance=270 package=THT]
  9V = Voltage Regulator - Variable [package="TO220 [THT]"]
  C3 = Electrolytic Capacitor [capacitance=1µF package="100 mil [THT, electrolytic]"]
  12v_Solar_Panel = SOLAR-IXYS [package=solarbit-12x1]
  U1 = LIPO-2000mAh [package=lipo-2000]
  U3 = LIPO-2000mAh [package=lipo-2000]
  U2 = LIPO-2000mAh [package=lipo-2000]
  Power_plug1 = Power plug
  PWR_2 = female pin header, 2 pins [form="♀ (female)"]
  S2 = Pushbutton [package=THT]  # not connected
  B1 = female pin header, 1 pin [form="♀ (female)"]
  B- = female pin header, 1 pin [form="♀ (female)"]
  B2 = female pin header, 1 pin [form="♀ (female)"]
  B+ = female pin header, 1 pin [form="♀ (female)"]
  P+ = female pin header, 1 pin [form="♀ (female)"]
  P- = female pin header, 1 pin [form="♀ (female)"]

nets:
  GND: BMP280.pin1, UV.pin3, PWR_LED.pin1, Tx_LED.pin1, Rain.pin2, W_Dir.pin2, Wind_2.pin2, C2.-, R2.leg1, 5v.GND, C1.-, R5.Pin_0, Arduino_Nano.GND, UART.pin3, RST.pin2, ESP_8266.GND, R4.leg1, C4.-, C3.-, PWR_2.pin2
  3.3V: BMP280.pin2, UV.pin1, UV.pin4, R6.Pin_0, 3_3V.OUT, R1.Pin_0, C2.+, Arduino_Nano.A3, ESP_8266.VCC, R7.Pin_0
  N1: BMP280.pin3, Arduino_Nano.A4
  N2: BMP280.pin4, Arduino_Nano.A5
  N3: UV.pin2, Arduino_Nano.A2
  N4: PWR_LED.pin2, R7.Pin_1
  N5: Tx_LED.pin2, Arduino_Nano.D13/SCK
  N6: R6.Pin_1, ESP_8266.CH_PD
  N7: Rain.pin1, R9.Pin_1, Arduino_Nano.D2
  5V: Rain.pin3, W_Dir.pin3, Wind_2.pin3, R9.Pin_0, R8.Pin_0, 5v.output_voltage, C3.+
  N8: W_Dir.pin1, Arduino_Nano.A0
  N9: 3_3V.ADJ, R1.Pin_1, R2.wiper, R2.leg2
  N10: 3_3V.IN, 5v.input_voltage, C1.+, 9V.IN, PWR_2.pin1
  N11: Wind_2.pin1, R8.Pin_1, Arduino_Nano.D3
  N12: R5.Pin_1, ESP_8266.GPIO_15
  N13: Arduino_Nano.D10, UART.pin2, ESP_8266.RXD
  N14: Arduino_Nano.D11/MOSI, UART.pin1, ESP_8266.TXD
  9V: Arduino_Nano.VIN, C4.+, R3.Pin_0, 9V.OUT
  N15: RST.pin1, ESP_8266.GPIO_16, ESP_8266.REST
  N16: R4.wiper, R4.leg2, R3.Pin_1, 9V.ADJ
  N17: 12v_Solar_Panel.A, Power_plug1.VCC, P+.pin1
  N18: 12v_Solar_Panel.C, Power_plug1.GND, P-.pin1
  N19: U1.+, B-.pin1
  N20: U1.-, U2.+, B2.pin1
  N21: U3.+, U2.-, B1.pin1
  N22: U3.-, B+.pin1

notes:
  ML8511
  cjmcu-103
  3.3V
  9V
  Change 1.1 - Ground added, RX/TX changed to pin 10/11
  Change 1.2 Uart bridge added for serial monitor
  Weather Station, Arduino Nano and Esp 8266 Weather Station, 1.4
  Weather Station By S.Orton
  Change 1.3 Rain pin moved D5 to D2 (interupt pin)
  Change 1.3 WindSpd pin moved D6 to D3 (interupt pin)
  5V
  Change 1.4 Added 9Vdc regulator to power nano
  3.3vdc
  5vdc
  9vdc
  Rain Sensor
  SUPPLY VOLTAGES
  SENSORS
  MPU & WIFI
  Power LED (optional)
  Data Send LED
  Wind Speed Sensor
  Wind Direction Sensor
  UV Sensor
  Temp, Humidity Sensor
  3.3V ESP8266, BME280
  5V Wind Speed, Wind dir and Rain sensors
  9V Arduino
  ML8511 is powerd from Nano's 3v3 as the Nano uses the voltage to determine the uv level
  https://www.instructables.com/id/Arduino-Uno-Wireless-Weather-Station-Wundergroundc/
  With thanks to the following indistructable
  POWER OPTIONS
  3 x 18650 LiOn Batteries in series
  CHARGING OPTIONS
  BMS= Battery monitoring circuitboard available online
  Arduino Nano
  Hall Sensors and Cjmcu-103
  BME 280
  ESP 8266
  ML8511 powerd from Nano,s 3.3 volt line
  not this line
  Power input
  Connections relate to BMS 3S mangement board
  P+ and - are the battery power output
  and chargeing input
  Change 1.4 GPIO16 connect to rst for sleep wakeup
  Rev 1.4 30/12/19

// code stored in the sketch: Weather Stn v 1.3.ino

